# Fritzing sketch Stovetop-Alarm (saved by Fritzing 0.9.3b)
breadboards: 1

parts:
  LCD1 = LCD screen
  Melexis_90614 = MLX90614 [package=to-39]
  Part1 = Arduino Uno (Rev3) - ICSP
  R1 = Resistor [tolerance=±5% resistance=220 package="2512 [SMD]"]
  R2 = Resistor [tolerance=±5% resistance=220 package="2512 [SMD]"]

nets (from the breadboard view):
  VSS: LCD1.VSS, LCD1.R/W, LCD1.LED-, Melexis_90614.VSS, Part1.GND
  VDD: LCD1.VDD, Part1.5V
  N1: LCD1.V0, Part1.D5_PWM
  N2: LCD1.RS, Part1.D8
  N3: LCD1.E, Part1.D9_PWM
  N4: LCD1.DB4, Part1.D10_PWM/SS
  N5: LCD1.DB5, Part1.D11_PWM/MOSI
  N6: LCD1.DB6, Part1.D12/MISO
  N7: LCD1.DB7, Part1.D13/SCK
  N8: LCD1.LED+, Part1.D6_PWM
  N9: Melexis_90614.SCL_VZ, Part1.A5/SCL, R1.Pin_1
  N10: Melexis_90614.PWM_SDA, Part1.A4/SDA, R2.Pin_1
  VDD_2: Melexis_90614.VDD, Part1.3V3, R1.Pin_0, R2.Pin_0

notes:
  +3.3V rail for sensor
  +5V rail for LCD / everything else
