# Fritzing sketch Schematic (saved by Fritzing 0.9.1b)
breadboards: 1

parts:
  SONAR1 = Maxbotix MaxSonar Ultrasonic Sensor (Hi-Res)
  part = Maxbotix MaxSonar Ultrasonic Sensor (Hi-Res)  # not connected
  Part1 = Arduino Uno (Rev3)

nets:
  N1: SONAR1.AN, Part1.A0

custom parts:
  Maxbotix MaxSonar Ultrasonic Sensor (Hi-Res): Maxbotix MaxSonar Hi-Resolution Ultrasonic Sensor HRLV-EZ0, HRLV-EZ1, HRLV-EZ2, HRLV-EZ3, HRLV-EZ4
